# Fritzing sketch PBB_ESP32_S3 (saved by Fritzing 1.0.8)

parts:
  A2 = A4988 driver expansion card
  A3 = MAX6675 module [package=THT]
  M1 = ESP32-S3-DevKitC-1-N8R8-v1 [part_number=ESP32-S3-DevKitC-1-N8R8-v1]
  A4 = 4in spi lcd display
  Part1 = Adafruit DS3231 [part_number="Adafruit #3013"]  # not connected
  Part2 = Adafruit SHT31-D [part_number="Adafruit #2857"]
  RE1 = Rotary Encoder [package=THT]
  J1 = Piezo Speaker
  A5 = A4988 driver expansion card
  JL012-13-5_1 = JL012-13-5.2 Lever (Limit) Switch SPDT + NO + NC [part_number=JL012-13-5.2]
  A6 = MAX6675 module [package=THT]

nets:
  N1: A2.Pin_7, M1.pin_37
  N2: A2.Pin_8, M1.pin_35
  N3: A2.Pin_9, M1.pin_36
  N4: A3.pin1, M1.pin_22, M1.pin_23, M1.pin_44, A4.Pin_2, RE1.EncoderPinC
  N5: A3.pin2, M1.pin_1, M1.pin_2, A4.Pin_8
  N6: A3.pin3, M1.pin_10
  N7: A3.pin4, M1.pin_11
  N8: A3.pin5, M1.pin_27
  N9: M1.pin_4, Part2.SCL
  N10: M1.pin_5, Part2.SDA
  N11: M1.pin_6, A4.Pin_13
  N12: M1.pin_7, A4.Pin_12
  N13: M1.pin_8, A4.Pin_11
  N14: M1.pin_9, A4.Pin_14
  N15: M1.pin_12, A4.Pin_10
  N16: M1.pin_15, A4.Pin_9
  N17: M1.pin_16, A4.Pin_7
  N18: M1.pin_17, A4.Pin_6
  N19: M1.pin_18, A4.Pin_5
  N20: M1.pin_19, A4.Pin_4
  N21: M1.pin_20, A4.Pin_3
  N22: M1.pin_21, A4.Pin_1
  N23: M1.pin_26, JL012-13-5_1.NC
  N24: M1.pin_28, J1.pin2
  N25: M1.pin_38, A6.pin4
  N26: M1.pin_39, RE1.EncoderPinA
  N27: M1.pin_40, RE1.EncoderPinB
  N28: M1.pin_41, RE1.SwitchrPinD
  N29: M1.pin_42, A5.Pin_9
  N30: M1.pin_43, A5.Pin_8

notes:
  EC11 Rotary Pushbutton Encoder
  TMC2209 X-Motor
  Buzzer
  Real Time Clock
  SHT31 Ambient Temperature & Humidity Sensor
  MAX6675 #1
  Thermocouple
  ESP32-S3-WROOM-1 N8R8
  44-Pin ESP32-S3 Development Board
  ESP32-S3 44-PIN GPIO ASSIGNMENTS
  TFT / SPI
  GPIO 14 TFT_CS
  GPIO 13 TFT_RST
  GPIO 12 TFT_DC
  GPIO 11 SPI_MOSI
  GPIO 10 SPI_SCLK
  GPIO 09 SPI_MISO
  GPIO 16 SD_CS
  CAPACITIVE TOUCH
  GPIO 6 CTP_INT
  GPIO 7 CTP_SDA
  GPIO 8 CTP_SCL
  GPIO 15 CTP_RST
  MAX6675
  GPIO 17 MAX_SCK
  GPIO 18 MAX_CS
  GPIO 21 MAX_SO
  RTC DS3231 + SHT31
  (Shared I2C)
  GPIO 5 SDA
  GPIO 4 SCL
  EC11 ROTARY ENCODER
  GPIO 42 ENC_A
  GPIO 2 ENC_B
  GPIO 1 ENC_SW
  TMC2209 X-Motor
  GPIO 38 DIR
  GPIO 39 STEP
  GPIO 40 ENABLE
  BUZZER
  GPIO 47 BUZZER
  MAX6675 #2
  GPIO 17 MAX_SCK
  GPIO 41 MAX_CS
  GPIO 21 MAX_SO
  TMC2209 Y-Motor
  GPIO 44 DIR
  GPIO 43 STEP
  GPIO 40 ENABLE
  LIMIT SWITCH
  GPIO 20
  POWER
  3.3V RTC / SHT31 / MAX6675
  5V TFT
  GND COMMON GROUND
  TMC2209 Y-Motor
  MAX6675 #2
  Thermocouple
  ESP32-S3 GPIO / OPTIONAL COMPONENTS
  MAX6675 #1 (OPTIONAL)
  GPIO17 = SCK (shared)
  GPIO18 = CS
  GPIO21 = SO (shared)
  If not installed: GPIO18 becomes available.
  GPIO17/21 remain occupied if MAX6675 #2 is installed.
  If neither MAX6675 is installed: GPIO17/18/21 available.
  GPIO17/18 are also default UART1 TX/RX.
  MAX6675 #2 (OPTIONAL)
  GPIO17 = SCK (shared)
  GPIO41 = CS
  GPIO21 = SO (shared)
  If not installed: GPIO41 becomes available.
  GPIO17/21 remain occupied if MAX6675 #1 is installed.
  Y-MOTOR (OPTIONAL)
  GPIO43 = STEP
  GPIO44 = DIR
  GPIO40 = ENABLE (shared)
  If installed: default UART0 TX/RX unavailable.
  If not installed: GPIO43/44 available for default UART0.
  UART0 can be remapped to other GPIOs.
  LIMIT SWITCH (OPTIONAL)
  GPIO20 = LIMIT INPUT
  If installed: USB-JTAG unavailable.
  If not installed: GPIO20 available for USB-JTAG.
  USB-JTAG uses GPIO19/20.
  BUZZER
  GPIO47 = BUZZER
  GPIO47 has no current PBB alternate-function conflict.
  ESP32-S3 RESERVED / ALTERNATE FUNCTIONS
  JTAG / DEBUG
  GPIO39 = X STEP / JTAG MTCK
  GPIO40 = X/Y ENABLE / JTAG MTDO
  GPIO41 = MAX6675 #2 CS / JTAG MTDI
  GPIO42 = ENC_A / JTAG MTMS
  These pins are occupied by PBB hardware and
  cannot simultaneously be used for external JTAG.
  USB-JTAG
  GPIO19/20 = USB D-/D+
  GPIO20 is used by the optional Limit Switch.
  USB-JTAG therefore requires GPIO19/20 to remain free.
  ENCODER
  GPIO1 = ENC_SW / ADC1_CH0 / TOUCH1
  GPIO2 = ENC_B / ADC1_CH1 / TOUCH2
  GPIO42 = ENC_A / JTAG MTMS
  I2C
  GPIO4 = SCL / ADC1_CH3 / TOUCH4
  GPIO5 = SDA / ADC1_CH4 / TOUCH5
  TOUCH
  GPIO6-8 = CTP / Touch-capable GPIOs
  GPIO15 = CTP_RST / ADC2_CH4 / U0RTS / XTAL_32K
  TFT / SPI
  GPIO9-14 and GPIO16 are occupied by TFT,
  Touch and SD functions.
  FLASH / PSRAM — N16R8
  GPIO26-37 = RESERVED FOR N16R8 FLASH/PSRAM
  This ESP32-S3-WROOM-1 N16R8 uses octal flash/PSRAM.
  GPIO26-37 are associated with internal memory
  and should not be used for external hardware.
  BOOT / STRAPPING PINS
  GPIO0, GPIO3, GPIO45, GPIO46
  Avoid external circuitry that could force these
  pins to the wrong level during reset/boot.
  IMPORTANT
  ESP32-S3 peripheral signals can generally be
  remapped to other available GPIOs through the
  GPIO matrix.
  Limitations listed here apply to the CURRENT
  PBB hardware configuration. Removing an optional
  component may free its GPIO and associated
  default peripheral function unless that GPIO is
  also used elsewhere or is reserved.

custom parts:
  A4988 driver expansion card: A4988 driver expansion card.
  MAX6675 module: MAX6675 Module + K Type Thermocouple Sensor Temperature Degrees.
  ESP32-S3-DevKitC-1-N8R8-v1: ESP32-S3-DevKitC-1-N8R8-v1 This module is 44pins long (2x22) and 11 pins width.
  4in spi lcd display: 4.0inch color screen with 320x480 resolution of 65K colors and rich display colors.
  Adafruit SHT31-D: Sensirion Temperature/Humidity sensors are some of the finest & highest-accuracy devices you can get. And, finally we have some that have a true I2C interface for easy reading. The SHT31-D sensor has an excellent ±2% relative humidity and ±0.3°C accuracy for most uses. We now use the version with a PTFE filter, it'll stay clean while still allowing humidity measurements to work Unlike earlier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
  Rotary Encoder: Rotary Encoder from ALPSec11e with switch.
  JL012-13-5.2 Lever (Limit) Switch SPDT + NO + NC: Micro Switch; Model No.: JL012-13.5-2; Actuator Action: Momentary; Actuator Type: Hinge Lever; Contact Configuration: 1NO, 1NC (SPDT) Temperature -25~65℃；Relative humidity: below 85%; Rate Voltage: 125V AC; Rated Current: 1A.
