# Fritzing sketch PBB_UNO_TFT_35_Display_UI (saved by Fritzing 1.0.8)
breadboards: 1

parts:
  Part2 = LilyPad Button Board  # not connected
  Part3 = LilyPad Button Board  # not connected
  Part4 = LilyPad Button Board  # not connected
  Part5 = LilyPad Button Board  # not connected
  LED1 = LED - 3mm [color="Red (633nm)" current=0.030A package="3 mm [THT]"]
  J1 = Piezo Speaker
  R7 = Resistor [tolerance=±5% resistance=220 package="0805 [SMD]"]
  S1 = Round Pushbutton
  S2 = Round Pushbutton
  A1 = MAX6675 module [package=THT]
  A2 = Arduino R4 Minima
  LCD1 = TFT 3.5 inch 480x320 w touch and SD

nets:
  N1: LED1.cathode, A2.Pin_40
  N2: LED1.anode, R7.Pin_0
  N3: J1.pin1, R7.Pin_1, S1.leg1, S2.leg1, A1.pin1, A2.Pin_6, A2.Pin_17, A2.Pin_45, LCD1.Pin_2
  N4: J1.pin2, A2.Pin_41
  N5: S1.leg0, A2.Pin_43
  N6: S2.leg0, A2.Pin_42
  N7: A1.pin2, A2.Pin_5, LCD1.Pin_1, LCD1.Pin_8
  N8: A1.pin3, A2.Pin_11
  N9: A1.pin4, A2.Pin_10
  N10: A1.pin5, A2.Pin_9
  N11: A2.Pin_12, LCD1.Pin_5
  N12: A2.Pin_13, LCD1.Pin_4
  N13: A2.Pin_14, LCD1.Pin_3
  N14: A2.Pin_35, LCD1.Pin_6
  N15: A2.Pin_38, LCD1.Pin_7

notes:
  RPM
  + LCD Reset
  Timer
  + Reset Timer
  Buzzer
  LED
  MAX6675
  Thermocouple
  Stepper motor and driver wiring intentionally omitted.
  LED current-limit resistor:
  ~220Ω (150–330Ω acceptable)
  Resistor values shown are typical; exact values are not critical.
  MAX6675
  SO A2
  CS A1
  SCK A0
  RPM D12
  Timer D11
  Buzz D10
  LED D9
  TFT
  CS A5
  RST A4
  DC A3
  MOSI D4
  SCK D7
  VCC 5V
  GND GND
  LED 5V

custom parts:
  Round Pushbutton: A generic pushbutton.
  MAX6675 module: MAX6675 Module + K Type Thermocouple Sensor Temperature Degrees.
  Arduino R4 Minima: Introducing the Arduino UNO R4 Minima! This board boasts the RA4M1 microprocessor from Renesas, delivering increased processing power, expanded memory, and additional peripherals.
  TFT 3.5 inch 480x320 w touch and SD: This is a generic 1.8 tft spi lcd display available on ebay and others. The 1.8"3.5 inch 480X320 SPI TFT Module 320x480 LCD Display - Touch.
