# Fritzing sketch Planetary_Bean_Bouncer_UNO_UI (saved by Fritzing 1.0.7)
breadboards: 1

parts:
  Part1 = LCD1602-I2C
  Part2 = LilyPad Button Board  # not connected
  Part3 = LilyPad Button Board  # not connected
  Part4 = LilyPad Button Board  # not connected
  Part5 = LilyPad Button Board  # not connected
  LED1 = LED - 3mm [color="Red (633nm)" current=0.030A package="3 mm [THT]"]
  J1 = Piezo Speaker
  R7 = Resistor [tolerance=±5% resistance=220 package="0805 [SMD]"]
  S1 = Round Pushbutton
  S2 = Round Pushbutton
  S3 = Round Pushbutton
  S4 = Round Pushbutton
  Part6 = Arduino Ethernet Shield (Rev3)
  A1 = MAX6675 module [package=THT]

nets:
  GND: Part1.GND, J1.pin1, R7.Pin_1, S1.leg1, S2.leg1, S3.leg1, S4.leg1, Part6.GND, A1.pin1
  VCC: Part1.VCC, Part6.5V
  N1: Part1.SDA, Part6.A4/SDA
  N2: Part1.SCL, Part6.A5/SCL
  N3: LED1.cathode, Part6.D7
  N4: LED1.anode, R7.Pin_0
  N5: J1.pin2, Part6.PWM_D9
  N6: S1.leg0, Part6.SPI/D13
  N7: S2.leg0, Part6.SPI/D12
  N8: S3.leg0, Part6.PWM_D11
  N9: S4.leg0, Part6.ETH_CS
  N10: Part6.A0, A1.pin3
  N11: Part6.A1, A1.pin4
  N12: Part6.A2, A1.pin5

notes:
  RPM
  + LCD Reset
  Timer
  + Reset Timer
  Profile
  + LCD Reset
  CW/CCW
  + Buzzer Mute
  I2C LCD
  Buzzer
  LED
  MAX6675
  Thermocouple
  Arduino UNO
  Stepper motor and driver wiring intentionally omitted.
  LED current-limit resistor:
  ~220Ω (150–330Ω acceptable)
  Resistor values shown are typical; exact values are not critical.

custom parts:
  LCD1602-I2C: A standard character display, usually with 2x16 characters. Comes in many colors with LCM1602 IIC attached.
  Round Pushbutton: A generic pushbutton.
  MAX6675 module: MAX6675 Module + K Type Thermocouple Sensor Temperature Degrees.
